# Fritzing sketch Wetterstation (saved by Fritzing 0.9.3b)
circuit board: 9.3cm x 6.39cm
breadboards: 1

parts:
  R2 = Resistor [tolerance=±1% resistance=10k package=THT]
  DHT = DHT22 Humidity and Temperature Sensor
  R4 = Resistor [tolerance=±1% resistance=33k package=THT]
  V+ = Header 1 [package=1x01_offset]
  Pololu = Pololu 5V Step-Up Regulator
  V- = Header 1 [package=1x01_offset]
  Akku+ = Header 1 [package=1x01_offset]
  Windsensor = Header 1 [package=1x01_offset]
  Windsensor_2 = Header 1 [package=1x01_offset]
  R1 = Resistor [tolerance=±1% resistance=10k package=THT]
  T1 = NPN-Transistor [part_number="BC 337-40" package="TO92 [THT]"]
  R5 = Resistor [tolerance=±1% resistance=10k package=THT]
  R3 = Resistor [tolerance=±1% resistance=33k package=THT]
  Akku_- = Header 1 [package=1x01_offset]
  MKR1000 = Arduino MKR1000
  DS1 = DS18B20 1-Wire Temperature Sensor [part_number=DS18B20]
  DS2 = DS18B20 1-Wire Temperature Sensor [part_number=DS18B20]
  BMP180 = BMP180 Breakout (GY-68)

nets (from the pcb view):
  VDD: R2.Pin_0, DHT.VDD, R1.Pin_0, MKR1000.VCC, DS1.VDD, DS2.VDD, BMP180.VCC
  N1: R2.Pin_1, MKR1000.D0, DS1.DQ, DS2.DQ
  N2: DHT.DATA, R1.Pin_1, MKR1000.D1
  GND: DHT.GND, Pololu.GND, V-.1, Windsensor.1, T1.E, R3.Pin_0, Akku_-.1, MKR1000.GND, DS1.GND, DS2.GND, BMP180.GND
  N3: R4.Pin_0, Akku+.1
  N4: R4.Pin_1, R3.Pin_1, MKR1000.A0_DAC0
  N5: V+.1, Pololu.VIN
  N6: Pololu.VOUT, MKR1000.VIN
  N7: Windsensor_2.1, MKR1000.D4_PWM
  N8: T1.B, R5.Pin_0
  N9: T1.C, MKR1000.RESET
  N10: R5.Pin_1, MKR1000.D7
  N11: MKR1000.D11_SDA, BMP180.SDA
  N12: MKR1000.D12_SCL, BMP180.SCL

notes:
  Wetterstation v1.0

custom parts:
  Arduino MKR1000: MKR1000 is a powerful board that combines the functionality of the Zero and the Wi-Fi Shield. It is the ideal solution for makers wanting to design IoT projects with minimal previous experience in networking
  BMP180 Breakout (GY-68): This is a simple breakout board for the BMP180, a high-precision, low-power barometric pressure sensor made by Bosch Sensortec. The range of measurement is from 300hPa to 1100hPa. The sensor can be supplied with voltage ranging from 1.8V to 3.6V. Operating temperature range is -40 to +85 °C. This particular breakout board (or perhaps the configuration) is produced by Shenzhen Keep Power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
